# Fritzing sketch stepperMotor (saved by Fritzing 0.9.4)
breadboards: 1

parts:
  Part1 = Arduino Micro (Rev3)
  LED1 = LED - 5mm [color="Yellow (595nm)" package="5 mm [THT]"]
  LED2 = LED - 5mm [color="Red (633nm)" package="5 mm [THT]"]
  R1 = Resistor [tolerance=±5% resistance=330 package=THT]
  R2 = Resistor [tolerance=±5% resistance=220 package=THT]
  S1 = Pushbutton [package="[THT]"]
  MD03A1 = Dual VNH2SP30 Motor Driver [part_number=MD03A]
  VCC1 = Battery block 9V
  M1 = Stepper Motor - Unipolar

nets:
  N1: Part1.D1/TX, LED2.cathode, S1.Pin_3, S1.Pin_4, VCC1.-
  N2: Part1.D2/SDA, S1.Pin_1, S1.Pin_2
  N3: Part1.D8_PWM/A8, MD03A1.1INa
  N4: Part1.D9_PWM/A9, MD03A1.1INb
  N5: Part1.D10_PWM/A10, MD03A1.PWM
  N6: Part1.D11_PWM, MD03A1.1CS
  N7: Part1.AREF, LED1.cathode, VCC1.+
  N8: LED1.anode, R1.Pin_0
  N9: LED2.anode, R2.Pin_0
  N10: MD03A1.OUT_1A, M1.D
  N11: MD03A1.OUT_1B, M1.B
  N12: MD03A1.OUT_2A, M1.C
  N13: MD03A1.OUT_2B, M1.A
  N14: MD03A1.GND, M1.COMMON_2
